// Logisim project alu_1bit.circ as structural Verilog: 2 circuits, main circuit main
module main (
  input  in_1,
  input  [2:0] in_2,
  input  [3:0] in_3,
  input  [3:0] in_4,
  input  a,
  input  b,
  input  o2,
  input  o1,
  input  o0,
  input  cin,
  output [3:0] out_11,
  output out_12,
  output r,
  output cout
);

  wire adder_1_out, alu_1bit_1_cout, alu_1bit_2_cout, alu_1bit_3_cout, and_1_out, multiplexer_1_out,
       not_1_out, or_1_out, or_2_out;

  Multiplexer #(.select(1), .width(1)) multiplexer_1 (
    .in0(b), .in1(not_1_out), .out(multiplexer_1_out), .sel(or_1_out));
  not not_1 (not_1_out, b);
  or or_1 (or_1_out, o2, cin);
  alu_1bit alu_1bit_1 (
    .a(in_3[0]), .b(in_4[0]), .cin(in_1), .o2(in_2[2]), .o1(in_2[1]), .o0(in_2[0]), .r(out_11[0]),
    .cout(alu_1bit_1_cout));
  alu_1bit alu_1bit_2 (
    .a(in_3[1]), .b(in_4[1]), .cin(alu_1bit_1_cout), .o2(in_2[2]), .o1(in_2[1]), .o0(in_2[0]), .r(out_11[1]),
    .cout(alu_1bit_2_cout));
  alu_1bit alu_1bit_3 (
    .a(in_3[2]), .b(in_4[2]), .cin(alu_1bit_2_cout), .o2(in_2[2]), .o1(in_2[1]), .o0(in_2[0]), .r(out_11[2]),
    .cout(alu_1bit_3_cout));
  alu_1bit alu_1bit_4 (
    .a(in_3[3]), .b(in_4[3]), .cin(alu_1bit_3_cout), .o2(in_2[2]), .o1(in_2[1]), .o0(in_2[0]), .r(out_11[3]),
    .cout(out_12));
  and and_1 (and_1_out, a, multiplexer_1_out);
  or or_2 (or_2_out, a, multiplexer_1_out);
  Adder #(.width(1)) adder_1 (.a(a), .b(multiplexer_1_out), .out(adder_1_out), .cin(or_1_out), .cout(cout));
  Multiplexer #(.select(3), .width(1)) multiplexer_2 (
    .in0(and_1_out), .in1(or_2_out), .in2(adder_1_out), .in6(adder_1_out), .in7(cout), .out(r),
    .sel({o2, o1, o0}));  // open: in3, in4, in5
endmodule

module alu_1bit (
  input  a,
  input  b,
  input  o2,
  input  o1,
  input  o0,
  input  cin,
  output r,
  output cout
);

  wire adder_1_out, and_1_out, multiplexer_1_out, not_1_out, not_2_out, or_1_out, or_2_out, xor_1_out;

  xor xor_1 (xor_1_out, a, b);
  Multiplexer #(.select(1), .width(1)) multiplexer_1 (.in0(b), .in1(not_1_out), .out(multiplexer_1_out), .sel(o2));
  not not_1 (not_1_out, b);
  or or_1 (or_1_out, o2, cin);
  and and_1 (and_1_out, a, multiplexer_1_out);
  or or_2 (or_2_out, a, multiplexer_1_out);
  Adder #(.width(1)) adder_1 (.a(a), .b(multiplexer_1_out), .out(adder_1_out), .cin(or_1_out), .cout(cout));
  not not_2 (not_2_out, a);
  Multiplexer #(.select(3), .width(1)) multiplexer_2 (
    .in0(and_1_out), .in1(or_2_out), .in2(adder_1_out), .in3(xor_1_out), .in4(not_2_out), .in6(adder_1_out),
    .in7(cout), .out(r), .sel({o2, o1, o0}));  // open: in5
endmodule
