// Logisim project alu_6bit.circ as structural Verilog: 2 circuits, main circuit main
module main (
  input  [2:0] OPCODE,
  input  [5:0] A,
  input  [5:0] B,
  input  crw,
  input  clk,
  output [5:0] DATA_OUT,
  output Z,
  output CARRY_OUT
);

  wire alu_1bit_1_cout, alu_1bit_2_cout, alu_1bit_3_cout, alu_1bit_4_cout, alu_1bit_5_cout, and_1_out,
       and_2_out, d_ff_1_q, nor_1_out;

  alu_1bit alu_1bit_1 (
    .a(A[0]), .b(B[0]), .cin(and_1_out), .o2(OPCODE[2]), .o1(OPCODE[1]), .o0(OPCODE[0]), .r(DATA_OUT[0]),
    .cout(alu_1bit_1_cout));
  alu_1bit alu_1bit_2 (
    .a(A[1]), .b(B[1]), .cin(alu_1bit_1_cout), .o2(OPCODE[2]), .o1(OPCODE[1]), .o0(OPCODE[0]),
    .r(DATA_OUT[1]), .cout(alu_1bit_2_cout));
  alu_1bit alu_1bit_3 (
    .a(A[2]), .b(B[2]), .cin(alu_1bit_2_cout), .o2(OPCODE[2]), .o1(OPCODE[1]), .o0(OPCODE[0]),
    .r(DATA_OUT[2]), .cout(alu_1bit_3_cout));
  alu_1bit alu_1bit_4 (
    .a(A[3]), .b(B[3]), .cin(alu_1bit_3_cout), .o2(OPCODE[2]), .o1(OPCODE[1]), .o0(OPCODE[0]),
    .r(DATA_OUT[3]), .cout(alu_1bit_4_cout));
  alu_1bit alu_1bit_5 (
    .a(A[4]), .b(B[4]), .cin(alu_1bit_4_cout), .o2(OPCODE[2]), .o1(OPCODE[1]), .o0(OPCODE[0]),
    .r(DATA_OUT[4]), .cout(alu_1bit_5_cout));
  alu_1bit alu_1bit_6 (
    .a(A[5]), .b(B[5]), .cin(alu_1bit_5_cout), .o2(OPCODE[2]), .o1(OPCODE[1]), .o0(OPCODE[0]),
    .r(DATA_OUT[5]), .cout(CARRY_OUT));
  and and_1 (and_1_out, OPCODE[1], OPCODE[0], d_ff_1_q);
  and and_2 (and_2_out, crw, clk);
  D_Flip_Flop #(.trigger("falling")) d_ff_1 (.clk(and_2_out), .Q(d_ff_1_q));  // open: D, Qn, preset, en, reset
  nor nor_1 (nor_1_out, DATA_OUT[0], DATA_OUT[1], DATA_OUT[2], DATA_OUT[3], DATA_OUT[4]);
  or or_1 (Z, nor_1_out, DATA_OUT[5]);
endmodule

module alu_1bit (
  input  a,
  input  b,
  input  o2,
  input  o1,
  input  o0,
  input  cin,
  output r,
  output cout
);

  wire adder_1_out, and_1_out, multiplexer_1_out, not_1_out, not_2_out, or_1_out, or_2_out, xor_1_out;

  xor xor_1 (xor_1_out, a, b);
  Multiplexer #(.select(1), .width(1)) multiplexer_1 (.in0(b), .in1(not_1_out), .out(multiplexer_1_out), .sel(o2));
  not not_1 (not_1_out, b);
  or or_1 (or_1_out, o2, cin);
  and and_1 (and_1_out, a, multiplexer_1_out);
  or or_2 (or_2_out, a, multiplexer_1_out);
  Adder #(.width(1)) adder_1 (.a(a), .b(multiplexer_1_out), .out(adder_1_out), .cin(or_1_out), .cout(cout));
  not not_2 (not_2_out, a);
  Multiplexer #(.select(3), .width(1)) multiplexer_2 (
    .in0(and_1_out), .in1(or_2_out), .in2(adder_1_out), .in3(adder_1_out), .in4(not_2_out), .in5(xor_1_out),
    .in6(adder_1_out), .in7(adder_1_out), .out(r), .sel({o2, o1, o0}));
endmodule
