// Logisim project CURRENT_TO_CONTROL.circ as structural Verilog: 1 circuit, main circuit main
module main (
  input  [3:0] in_1,
  output PCML,
  output PCMH,
  output PCW,
  output MASM,
  output MW,
  output IRW,
  output AML,
  output AMH,
  output AW,
  output DRW,
  output ALUAM,
  output ALUBM,
  output ALUOM,
  output CRW
);

  wire decoder_1_out1, decoder_1_out3, decoder_1_out8, decoder_1_out9, or_2_out;

  Decoder #(.select(4), .tristate("false")) decoder_1 (
    .out0(ALUAM), .out1(decoder_1_out1), .out2(DRW), .out3(decoder_1_out3), .out4(CRW), .out5(AML),
    .out6(AMH), .out7(MW), .out8(decoder_1_out8), .out9(decoder_1_out9), .out10(PCMH), .sel(in_1));  // open: out11, out12, out13, out14, out15
  or or_1 (PCW, ALUAM, decoder_1_out9, PCMH);
  or or_2 (or_2_out, decoder_1_out3, CRW, AML);
  or or_3 (AW, or_2_out, AMH);

  assign ALUBM = ALUAM;
  assign ALUOM = ALUAM;
  assign IRW = ALUAM;
  assign MASM = ALUAM;
  assign PCML = ALUAM;
endmodule
