// Logisim project NS0.circ as structural Verilog: 6 circuits, main circuit main
module main (
  input  [3:0] O_OPCODE,
  input  Z,
  input  M,
  input  C,
  input  CLK,
  output [3:0] CURRENT_STATE
);

  wire [3:0] ns0_1_ns0;

  SR sr_1 (.CLK(CLK), .INPUT(ns0_1_ns0), .OUTPUT(CURRENT_STATE));
  NS0 ns0_1 (
    .CS0(CURRENT_STATE[0]), .CS1(CURRENT_STATE[1]), .CS2(CURRENT_STATE[2]), .CS3(CURRENT_STATE[3]),
    .O0(O_OPCODE[0]), .O1(O_OPCODE[1]), .O2(O_OPCODE[2]), .O3(O_OPCODE[3]), .Z(Z), .M(M), .C(C),
    .NS0(ns0_1_ns0[0]));
  NS1 ns1_1 (
    .CS0(CURRENT_STATE[0]), .CS1(CURRENT_STATE[1]), .CS2(CURRENT_STATE[2]), .CS3(CURRENT_STATE[3]),
    .O0(O_OPCODE[0]), .O1(O_OPCODE[1]), .O2(O_OPCODE[2]), .O3(O_OPCODE[3]), .Z(Z), .M(M), .C(C),
    .NS1(ns0_1_ns0[1]));
  NS2 ns2_1 (
    .CS0(CURRENT_STATE[0]), .CS1(CURRENT_STATE[1]), .CS2(CURRENT_STATE[2]), .CS3(CURRENT_STATE[3]),
    .O0(O_OPCODE[0]), .O1(O_OPCODE[1]), .O2(O_OPCODE[2]), .O3(O_OPCODE[3]), .Z(Z), .M(M), .C(C),
    .NS2(ns0_1_ns0[2]));
  NS3 ns3_1 (
    .CS0(CURRENT_STATE[0]), .CS1(CURRENT_STATE[1]), .CS2(CURRENT_STATE[2]), .CS3(CURRENT_STATE[3]),
    .O0(O_OPCODE[0]), .O1(O_OPCODE[1]), .O2(O_OPCODE[2]), .O3(O_OPCODE[3]), .Z(Z), .M(M), .C(C),
    .NS3(ns0_1_ns0[3]));
endmodule

module NS0 (
  input  CS0,
  input  CS1,
  input  CS2,
  input  CS3,
  input  O0,
  input  O1,
  input  O2,
  input  O3,
  input  Z,
  input  M,
  input  C,
  output NS0
);

  wire and_1_out, and_2_out, and_3_out, and_4_out, and_5_out, and_6_out, and_7_out, and_8_out, and_9_out,
       and_10_out, and_11_out, and_12_out, and_13_out, and_14_out, and_15_out, and_16_out, and_17_out,
       and_18_out, and_19_out, not_1_out, not_2_out, not_3_out, not_4_out, not_5_out, not_6_out, not_7_out,
       not_8_out, not_9_out, not_10_out, not_11_out, not_12_out, not_13_out, not_14_out, not_15_out,
       not_16_out, not_17_out, not_18_out, not_19_out, not_20_out, not_21_out, not_22_out, not_23_out,
       not_24_out, not_25_out, not_26_out, not_27_out, not_28_out, not_29_out, not_30_out, not_31_out,
       not_32_out, not_33_out, not_34_out, not_35_out, not_36_out, not_37_out, not_38_out, not_39_out,
       not_40_out, not_41_out, not_42_out, not_43_out, not_44_out, not_45_out, not_46_out, not_47_out,
       not_48_out, not_49_out, not_50_out, not_51_out, not_52_out, not_53_out, not_54_out, not_55_out,
       not_56_out, not_57_out, not_58_out, not_59_out, not_60_out, not_61_out, not_62_out, not_63_out,
       not_64_out, not_65_out, not_66_out, not_67_out, not_68_out, not_69_out, not_70_out, not_71_out,
       not_72_out, not_73_out, not_74_out, not_75_out, not_76_out, not_77_out, not_78_out, not_79_out,
       not_80_out, not_81_out, not_82_out, not_83_out, not_84_out, not_85_out, not_86_out, not_87_out,
       not_88_out, not_89_out, not_90_out, not_91_out, not_92_out, not_93_out, not_94_out, not_95_out,
       or_1_out, or_2_out, or_3_out;

  not not_1 (not_1_out, CS1);
  not not_2 (not_2_out, CS2);
  not not_3 (not_3_out, CS3);
  not not_4 (not_4_out, O0);
  not not_5 (not_5_out, O1);
  not not_6 (not_6_out, O2);
  not not_7 (not_7_out, CS1);
  not not_8 (not_8_out, CS2);
  not not_9 (not_9_out, CS3);
  not not_10 (not_10_out, O1);
  not not_11 (not_11_out, O2);
  not not_12 (not_12_out, CS1);
  not not_13 (not_13_out, CS2);
  not not_14 (not_14_out, CS3);
  not not_15 (not_15_out, O2);
  not not_16 (not_16_out, CS1);
  not not_17 (not_17_out, CS2);
  not not_18 (not_18_out, CS3);
  not not_19 (not_19_out, O1);
  not not_20 (not_20_out, CS1);
  not not_21 (not_21_out, CS2);
  not not_22 (not_22_out, CS3);
  not not_23 (not_23_out, CS0);
  not not_24 (not_24_out, CS2);
  not not_25 (not_25_out, CS3);
  not not_26 (not_26_out, O0);
  not not_27 (not_27_out, O1);
  not not_28 (not_28_out, O2);
  not not_29 (not_29_out, O3);
  not not_30 (not_30_out, CS0);
  not not_31 (not_31_out, CS2);
  not not_32 (not_32_out, CS3);
  not not_33 (not_33_out, O1);
  not not_34 (not_34_out, O2);
  not not_35 (not_35_out, O3);
  not not_36 (not_36_out, CS0);
  not not_37 (not_37_out, CS2);
  not not_38 (not_38_out, CS3);
  not not_39 (not_39_out, O0);
  not not_40 (not_40_out, O2);
  not not_41 (not_41_out, O3);
  not not_42 (not_42_out, CS0);
  not not_43 (not_43_out, CS2);
  not not_44 (not_44_out, CS3);
  not not_45 (not_45_out, O2);
  not not_46 (not_46_out, O3);
  not not_47 (not_47_out, CS1);
  not not_48 (not_48_out, CS2);
  not not_49 (not_49_out, CS3);
  not not_50 (not_50_out, O0);
  not not_51 (not_51_out, O1);
  not not_52 (not_52_out, O2);
  not not_53 (not_53_out, CS1);
  not not_54 (not_54_out, CS2);
  not not_55 (not_55_out, CS3);
  not not_56 (not_56_out, O1);
  not not_57 (not_57_out, O2);
  not not_58 (not_58_out, CS1);
  not not_59 (not_59_out, CS2);
  not not_60 (not_60_out, CS3);
  not not_61 (not_61_out, O2);
  not not_62 (not_62_out, CS1);
  not not_63 (not_63_out, CS2);
  not not_64 (not_64_out, CS3);
  not not_65 (not_65_out, O1);
  not not_66 (not_66_out, CS1);
  not not_67 (not_67_out, CS2);
  not not_68 (not_68_out, CS3);
  not not_69 (not_69_out, CS0);
  not not_70 (not_70_out, CS2);
  not not_71 (not_71_out, CS3);
  not not_72 (not_72_out, O0);
  not not_73 (not_73_out, O1);
  not not_74 (not_74_out, O2);
  not not_75 (not_75_out, O3);
  not not_76 (not_76_out, CS0);
  not not_77 (not_77_out, CS2);
  not not_78 (not_78_out, CS3);
  not not_79 (not_79_out, O1);
  not not_80 (not_80_out, O2);
  not not_81 (not_81_out, O3);
  not not_82 (not_82_out, CS0);
  not not_83 (not_83_out, CS2);
  not not_84 (not_84_out, CS3);
  not not_85 (not_85_out, O0);
  not not_86 (not_86_out, O2);
  not not_87 (not_87_out, O3);
  not not_88 (not_88_out, CS0);
  not not_89 (not_89_out, CS1);
  not not_90 (not_90_out, CS2);
  not not_91 (not_91_out, CS3);
  not not_92 (not_92_out, CS0);
  not not_93 (not_93_out, CS1);
  not not_94 (not_94_out, CS2);
  not not_95 (not_95_out, CS3);
  and and_1 (and_1_out, not_88_out, not_89_out, 1'b1, not_90_out, not_91_out);
  and and_2 (and_2_out, CS0, not_1_out, not_2_out, not_3_out, 1'b1, not_4_out, not_5_out, not_6_out, O3);
  and and_3 (and_3_out, CS0, not_7_out, not_8_out, not_9_out, 1'b1, O0, not_10_out, not_11_out, O3);
  and and_4 (and_4_out, CS0, not_12_out, not_13_out, not_14_out, 1'b1, O0, O1, not_15_out, O3);
  and and_5 (and_5_out, CS0, not_16_out, not_17_out, not_18_out, O0, not_19_out, O2, O3, Z);
  and and_6 (and_6_out, CS0, not_20_out, not_21_out, not_22_out, O0, O1, O2, O3, C);
  and and_7 (and_7_out, not_23_out, CS1, not_24_out, 1'b1, not_25_out, not_26_out, not_27_out, not_28_out, not_29_out);
  and and_8 (and_8_out, not_30_out, CS1, not_31_out, 1'b1, not_32_out, O0, not_33_out, not_34_out, not_35_out);
  and and_9 (and_9_out, not_36_out, CS1, not_37_out, 1'b1, not_38_out, not_39_out, O1, not_40_out, not_41_out);
  and and_10 (and_10_out, not_42_out, CS1, not_43_out, 1'b1, not_44_out, O0, O1, not_45_out, not_46_out);
  and and_11 (and_11_out, not_92_out, not_93_out, 1'b1, not_94_out, not_95_out);
  and and_12 (and_12_out, CS0, not_47_out, not_48_out, not_49_out, 1'b1, not_50_out, not_51_out, not_52_out, O3);
  and and_13 (and_13_out, CS0, not_53_out, not_54_out, not_55_out, 1'b1, O0, not_56_out, not_57_out, O3);
  and and_14 (and_14_out, CS0, not_58_out, not_59_out, not_60_out, 1'b1, O0, O1, not_61_out, O3);
  and and_15 (and_15_out, CS0, not_62_out, not_63_out, not_64_out, O0, not_65_out, O2, O3, Z);
  and and_16 (and_16_out, CS0, not_66_out, not_67_out, not_68_out, O0, O1, O2, O3, C);
  and and_17 (and_17_out, not_69_out, CS1, not_70_out, 1'b1, not_71_out, not_72_out, not_73_out, not_74_out, not_75_out);
  and and_18 (and_18_out, not_76_out, CS1, not_77_out, 1'b1, not_78_out, O0, not_79_out, not_80_out, not_81_out);
  and and_19 (and_19_out, not_82_out, CS1, not_83_out, 1'b1, not_84_out, not_85_out, O1, not_86_out, not_87_out);
  or or_1 (or_1_out, and_1_out, and_2_out, and_3_out, and_4_out, and_5_out, and_6_out, and_7_out);
  or or_2 (or_2_out, and_8_out, and_9_out, and_10_out, 1'b0, and_11_out, and_12_out, and_13_out);
  or or_3 (or_3_out, and_14_out, and_15_out, and_16_out, 1'b0, and_17_out, and_18_out, and_19_out);
  or or_4 (NS0, or_1_out, or_2_out, or_3_out);
endmodule

module NS1 (
  input  CS0,
  input  CS1,
  input  CS2,
  input  CS3,
  input  O0,
  input  O1,
  input  O2,
  input  O3,
  input  Z,
  input  M,
  input  C,
  output NS1
);

  wire and_1_out, and_2_out, and_3_out, and_4_out, and_5_out, and_6_out, not_1_out, not_2_out, not_3_out,
       not_4_out, not_5_out, not_6_out, not_7_out, not_8_out, not_9_out, not_10_out, not_11_out, not_12_out,
       not_13_out, not_14_out, not_15_out, not_16_out, not_17_out, not_18_out, not_19_out, not_20_out,
       not_21_out, not_22_out, not_23_out, not_24_out, not_25_out, not_26_out, not_27_out, not_28_out,
       not_29_out, not_30_out;

  not not_1 (not_1_out, CS1);
  not not_2 (not_2_out, CS2);
  not not_3 (not_3_out, CS3);
  not not_4 (not_4_out, O2);
  not not_5 (not_5_out, O3);
  not not_6 (not_6_out, CS1);
  not not_7 (not_7_out, CS2);
  not not_8 (not_8_out, CS3);
  not not_9 (not_9_out, O1);
  not not_10 (not_10_out, O3);
  not not_11 (not_11_out, CS0);
  not not_12 (not_12_out, CS2);
  not not_13 (not_13_out, CS3);
  not not_14 (not_14_out, O2);
  not not_15 (not_15_out, O3);
  not not_16 (not_16_out, CS1);
  not not_17 (not_17_out, CS2);
  not not_18 (not_18_out, CS3);
  not not_19 (not_19_out, O1);
  not not_20 (not_20_out, O2);
  not not_21 (not_21_out, CS1);
  not not_22 (not_22_out, CS2);
  not not_23 (not_23_out, CS3);
  not not_24 (not_24_out, O0);
  not not_25 (not_25_out, O2);
  not not_26 (not_26_out, CS1);
  not not_27 (not_27_out, CS2);
  not not_28 (not_28_out, CS3);
  not not_29 (not_29_out, O0);
  not not_30 (not_30_out, O1);
  and and_1 (and_1_out, CS0, not_1_out, not_2_out, 1'b1, not_3_out, not_4_out, not_5_out);
  and and_2 (and_2_out, CS0, not_6_out, not_7_out, not_8_out, not_9_out, O2, not_10_out);
  and and_3 (and_3_out, not_11_out, CS1, not_12_out, 1'b1, not_13_out, not_14_out, not_15_out);
  and and_4 (and_4_out, CS0, not_16_out, not_17_out, not_18_out, 1'b1, O0, not_19_out, not_20_out, O3);
  and and_5 (and_5_out, CS0, not_21_out, not_22_out, not_23_out, 1'b1, not_24_out, O1, not_25_out, O3);
  and and_6 (and_6_out, CS0, not_26_out, not_27_out, not_28_out, 1'b1, not_29_out, not_30_out, O2, O3);
  or or_1 (NS1, and_1_out, and_2_out, and_3_out, 1'b0, and_4_out, and_5_out, and_6_out);
endmodule

module NS2 (
  input  CS0,
  input  CS1,
  input  CS2,
  input  CS3,
  input  O0,
  input  O1,
  input  O2,
  input  O3,
  input  Z,
  input  M,
  input  C,
  output NS2
);

  wire and_1_out, and_2_out, and_3_out, and_4_out, not_1_out, not_2_out, not_3_out, not_4_out, not_5_out,
       not_6_out, not_7_out, not_8_out, not_9_out, not_10_out, not_11_out, not_12_out, not_13_out,
       not_14_out, not_15_out, not_16_out, not_17_out, not_18_out, not_19_out;

  not not_1 (not_1_out, CS0);
  not not_2 (not_2_out, CS2);
  not not_3 (not_3_out, CS3);
  not not_4 (not_4_out, O1);
  not not_5 (not_5_out, O3);
  not not_6 (not_6_out, CS0);
  not not_7 (not_7_out, CS2);
  not not_8 (not_8_out, CS3);
  not not_9 (not_9_out, O0);
  not not_10 (not_10_out, O3);
  not not_11 (not_11_out, CS1);
  not not_12 (not_12_out, CS2);
  not not_13 (not_13_out, CS3);
  not not_14 (not_14_out, O3);
  not not_15 (not_15_out, CS1);
  not not_16 (not_16_out, CS2);
  not not_17 (not_17_out, CS3);
  not not_18 (not_18_out, O1);
  not not_19 (not_19_out, O2);
  and and_1 (and_1_out, not_1_out, CS1, not_2_out, not_3_out, not_4_out, O2, not_5_out);
  and and_2 (and_2_out, not_6_out, CS1, not_7_out, not_8_out, 1'b1, not_9_out, O1, O2, not_10_out);
  and and_3 (and_3_out, CS0, not_11_out, not_12_out, not_13_out, 1'b1, O0, O1, O2, not_14_out);
  and and_4 (and_4_out, CS0, not_15_out, not_16_out, not_17_out, not_18_out, not_19_out, O3);
  or or_1 (NS2, and_1_out, and_2_out, 1'b0, and_3_out, and_4_out);
endmodule

module NS3 (
  input  CS0,
  input  CS1,
  input  CS2,
  input  CS3,
  input  O0,
  input  O1,
  input  O2,
  input  O3,
  input  Z,
  input  M,
  input  C,
  output NS3
);

  wire and_1_out, and_2_out, and_3_out, and_4_out, and_5_out, and_6_out, not_1_out, not_2_out, not_3_out,
       not_4_out, not_5_out, not_6_out, not_7_out, not_8_out, not_9_out, not_10_out, not_11_out, not_12_out,
       not_13_out, not_14_out, not_15_out, not_16_out, not_17_out, not_18_out, not_19_out, not_20_out,
       not_21_out;

  not not_1 (not_1_out, CS1);
  not not_2 (not_2_out, CS2);
  not not_3 (not_3_out, CS3);
  not not_4 (not_4_out, O2);
  not not_5 (not_5_out, CS1);
  not not_6 (not_6_out, CS2);
  not not_7 (not_7_out, CS3);
  not not_8 (not_8_out, O1);
  not not_9 (not_9_out, CS1);
  not not_10 (not_10_out, CS2);
  not not_11 (not_11_out, CS3);
  not not_12 (not_12_out, O0);
  not not_13 (not_13_out, CS1);
  not not_14 (not_14_out, CS2);
  not not_15 (not_15_out, CS3);
  not not_16 (not_16_out, CS1);
  not not_17 (not_17_out, CS2);
  not not_18 (not_18_out, CS3);
  not not_19 (not_19_out, O0);
  not not_20 (not_20_out, O1);
  not not_21 (not_21_out, CS3);
  and and_1 (and_1_out, CS0, CS1, 1'b1, CS2, not_21_out);
  and and_2 (and_2_out, CS0, not_1_out, not_2_out, not_3_out, 1'b1, O0, O1, not_4_out, O3);
  and and_3 (and_3_out, CS0, not_5_out, not_6_out, not_7_out, 1'b1, O0, not_8_out, O2, O3);
  and and_4 (and_4_out, CS0, not_9_out, not_10_out, not_11_out, 1'b1, not_12_out, O1, O2, O3);
  and and_5 (and_5_out, CS0, not_13_out, not_14_out, not_15_out, 1'b1, O0, O1, O2, O3);
  and and_6 (and_6_out, CS0, not_16_out, not_17_out, not_18_out, 1'b1, not_19_out, not_20_out, O2, O3);
  or or_1 (NS3, and_1_out, and_2_out, and_3_out, 1'b0, and_4_out, and_5_out, and_6_out);
endmodule

module SR (
  input  CLK,
  input  [3:0] INPUT,
  output [3:0] OUTPUT
);

  D_Flip_Flop #(.trigger("falling")) d_ff_1 (.clk(CLK), .D(INPUT[0]), .Q(OUTPUT[0]));  // open: Qn, preset, en, reset
  D_Flip_Flop #(.trigger("falling")) d_ff_2 (.clk(CLK), .D(INPUT[1]), .Q(OUTPUT[1]));  // open: Qn, preset, en, reset
  D_Flip_Flop #(.trigger("falling")) d_ff_3 (.clk(CLK), .D(INPUT[2]), .Q(OUTPUT[2]));  // open: Qn, preset, en, reset
  D_Flip_Flop #(.trigger("falling")) d_ff_4 (.clk(CLK), .D(INPUT[3]), .Q(OUTPUT[3]));  // open: Qn, preset, en, reset
endmodule
