// Logisim project DATAPATH.circ as structural Verilog: 4 circuits, main circuit main
module main (
  input  [9:0] DATA_IN,
  input  in_2,
  input  ZEROS,
  input  ONE,
  input  [2:0] in_5,
  input  [5:0] in_6,
  output [9:0] DATA_OUT
);

  wire main_3_aluam, main_3_alubm, main_3_aluom, main_3_aw, main_3_crw, main_3_drw, main_3_irw, main_3_masm,
       main_3_mw, main_3_pcw, main_8_carry_out, main_8_z, not_1_out;
  wire [1:0] main_3_aml, main_3_pcml;
  wire [2:0] main_7_alu_control, multiplexer_6_out;
  wire [3:0] main_2_current_state, main_5_opcode;
  wire [5:0] main_1_data_out, main_4_data_out, main_5_oprand, main_6_data_out, main_8_data_out,
       multiplexer_1_out, multiplexer_2_out, multiplexer_3_out, multiplexer_4_out, multiplexer_5_out;

  Clock #(.highDuration(1), .lowDuration(1)) CLK ();  // open: out
  Multiplexer #(.select(2), .width(6)) multiplexer_1 (
    .in0(main_5_oprand), .in1(main_8_data_out), .in2(DATA_OUT[9:4]), .out(multiplexer_1_out),
    .sel(main_3_pcml));  // open: in3
  program_counter_main main_1 (
    .in_1(in_2), .WRITEpc(main_3_pcw), .DATA_IN(multiplexer_1_out), .DATA_OUT(main_1_data_out));
  // Probe on main_1_data_out
  // Probe on main_2_current_state
  NS0_main main_2 (
    .O_OPCODE(main_5_opcode), .Z(main_8_z), .C(main_8_carry_out), .CLK(in_2),
    .CURRENT_STATE(main_2_current_state));  // open: M
  Multiplexer #(.select(1), .width(6)) multiplexer_2 (
    .in0(main_5_oprand), .in1(main_1_data_out), .out(multiplexer_2_out), .sel(main_3_masm));
  CURRENT_TO_CONTROL_main main_3 (
    .in_1(main_2_current_state), .PCML(main_3_pcml[0]), .PCMH(main_3_pcml[1]), .PCW(main_3_pcw),
    .MASM(main_3_masm), .MW(main_3_mw), .IRW(main_3_irw), .AML(main_3_aml[0]), .AMH(main_3_aml[1]),
    .AW(main_3_aw), .DRW(main_3_drw), .ALUAM(main_3_aluam), .ALUBM(main_3_alubm), .ALUOM(main_3_aluom),
    .CRW(main_3_crw));
  // Probe on multiplexer_2_out
  // Probe on DATA_OUT
  // Probe on DATA_OUT
  DATA_REGISTER_main main_4 (.CLK(in_2), .WRITE_IR(main_3_drw), .DATA_IN(DATA_OUT), .DATA_OUT(main_4_data_out));
  Multiplexer #(.select(2), .width(6)) multiplexer_3 (
    .in0(main_8_data_out), .in1(main_5_oprand), .in2(DATA_OUT[9:4]), .out(multiplexer_3_out), .sel(main_3_aml));  // open: in3
  instruction_register_main main_5 (
    .CLK(in_2), .WRITE_IR(main_3_irw), .DATA_IN(DATA_OUT), .opcode(main_5_opcode), .oprand(main_5_oprand));
  ACC_main main_6 (.CLK(in_2), .WRITE_IR(main_3_aw), .DATA_IN(multiplexer_3_out), .DATA_OUT(main_6_data_out));
  // Probe on main_6_data_out
  Multiplexer #(.select(1), .width(6)) multiplexer_4 (
    .in0(main_6_data_out), .in1(main_1_data_out), .out(multiplexer_4_out), .sel(main_3_aluam));
  Multiplexer #(.select(1), .width(6)) multiplexer_5 (
    .in0(main_4_data_out), .in1(in_6), .out(multiplexer_5_out), .sel(main_3_alubm));
  Multiplexer #(.select(1), .width(3)) multiplexer_6 (
    .in0(main_7_alu_control), .in1(in_5), .out(multiplexer_6_out), .sel(main_3_aluom));
  alu__control_main main_7 (.opcode(main_5_opcode), .alu_control(main_7_alu_control));
  // Probe on main_7_alu_control
  alu_6bit_main main_8 (
    .OPCODE(multiplexer_6_out), .A(multiplexer_4_out), .B(multiplexer_5_out), .crw(main_3_crw), .clk(in_2),
    .DATA_OUT(main_8_data_out), .Z(main_8_z), .CARRY_OUT(main_8_carry_out));
  not not_1 (not_1_out, in_2);
  RAM #(.addrWidth(6), .dataWidth(10), .bus("separate")) ram_1 (
    .addr(multiplexer_2_out), .din(DATA_IN), .data(DATA_OUT), .str(main_3_mw), .sel(ONE), .clk(not_1_out),
    .ld(ONE), .clr(ZEROS));

  // Notes on the sheet:
  //   DATA PATH STEP FIRST
endmodule

module CONROL_SIGNAL (
);

  wire [3:0] main_1_current_state;

  NS0_main main_1 (.CURRENT_STATE(main_1_current_state));  // open: O_OPCODE, Z, M, C, CLK
  CURRENT_TO_CONTROL_main main_2 (.in_1(main_1_current_state));  // open: PCML, PCMH, PCW, MASM, MW, IRW, AML, AMH, AW, DRW, ALUAM, ALUBM, ALUOM, CRW
endmodule

module NS0 (
  input  CS0,
  input  CS1,
  input  CS2,
  input  CS3,
  input  O0,
  input  O1,
  input  O2,
  input  O3,
  input  Z,
  input  M,
  input  C,
  output NS0
);

  wire and_1_out, and_2_out, and_3_out, and_4_out, and_5_out, and_6_out, and_7_out, and_8_out, and_9_out,
       and_10_out, and_11_out, and_12_out, and_13_out, and_14_out, and_15_out, and_16_out, and_17_out,
       and_18_out, and_19_out, not_1_out, not_2_out, not_3_out, not_4_out, not_5_out, not_6_out, not_7_out,
       not_8_out, not_9_out, not_10_out, not_11_out, not_12_out, not_13_out, not_14_out, not_15_out,
       not_16_out, not_17_out, not_18_out, not_19_out, not_20_out, not_21_out, not_22_out, not_23_out,
       not_24_out, not_25_out, not_26_out, not_27_out, not_28_out, not_29_out, not_30_out, not_31_out,
       not_32_out, not_33_out, not_34_out, not_35_out, not_36_out, not_37_out, not_38_out, not_39_out,
       not_40_out, not_41_out, not_42_out, not_43_out, not_44_out, not_45_out, not_46_out, not_47_out,
       not_48_out, not_49_out, not_50_out, not_51_out, not_52_out, not_53_out, not_54_out, not_55_out,
       not_56_out, not_57_out, not_58_out, not_59_out, not_60_out, not_61_out, not_62_out, not_63_out,
       not_64_out, not_65_out, not_66_out, not_67_out, not_68_out, not_69_out, not_70_out, not_71_out,
       not_72_out, not_73_out, not_74_out, not_75_out, not_76_out, not_77_out, not_78_out, not_79_out,
       not_80_out, not_81_out, not_82_out, not_83_out, not_84_out, not_85_out, not_86_out, not_87_out,
       not_88_out, not_89_out, not_90_out, not_91_out, not_92_out, not_93_out, not_94_out, not_95_out,
       or_1_out, or_2_out, or_3_out;

  not not_1 (not_1_out, CS1);
  not not_2 (not_2_out, CS2);
  not not_3 (not_3_out, CS3);
  not not_4 (not_4_out, O0);
  not not_5 (not_5_out, O1);
  not not_6 (not_6_out, O2);
  not not_7 (not_7_out, CS1);
  not not_8 (not_8_out, CS2);
  not not_9 (not_9_out, CS3);
  not not_10 (not_10_out, O1);
  not not_11 (not_11_out, O2);
  not not_12 (not_12_out, CS1);
  not not_13 (not_13_out, CS2);
  not not_14 (not_14_out, CS3);
  not not_15 (not_15_out, O2);
  not not_16 (not_16_out, CS1);
  not not_17 (not_17_out, CS2);
  not not_18 (not_18_out, CS3);
  not not_19 (not_19_out, O1);
  not not_20 (not_20_out, CS1);
  not not_21 (not_21_out, CS2);
  not not_22 (not_22_out, CS3);
  not not_23 (not_23_out, CS0);
  not not_24 (not_24_out, CS2);
  not not_25 (not_25_out, CS3);
  not not_26 (not_26_out, O0);
  not not_27 (not_27_out, O1);
  not not_28 (not_28_out, O2);
  not not_29 (not_29_out, O3);
  not not_30 (not_30_out, CS0);
  not not_31 (not_31_out, CS2);
  not not_32 (not_32_out, CS3);
  not not_33 (not_33_out, O1);
  not not_34 (not_34_out, O2);
  not not_35 (not_35_out, O3);
  not not_36 (not_36_out, CS0);
  not not_37 (not_37_out, CS2);
  not not_38 (not_38_out, CS3);
  not not_39 (not_39_out, O0);
  not not_40 (not_40_out, O2);
  not not_41 (not_41_out, O3);
  not not_42 (not_42_out, CS0);
  not not_43 (not_43_out, CS2);
  not not_44 (not_44_out, CS3);
  not not_45 (not_45_out, O2);
  not not_46 (not_46_out, O3);
  not not_47 (not_47_out, CS1);
  not not_48 (not_48_out, CS2);
  not not_49 (not_49_out, CS3);
  not not_50 (not_50_out, O0);
  not not_51 (not_51_out, O1);
  not not_52 (not_52_out, O2);
  not not_53 (not_53_out, CS1);
  not not_54 (not_54_out, CS2);
  not not_55 (not_55_out, CS3);
  not not_56 (not_56_out, O1);
  not not_57 (not_57_out, O2);
  not not_58 (not_58_out, CS1);
  not not_59 (not_59_out, CS2);
  not not_60 (not_60_out, CS3);
  not not_61 (not_61_out, O2);
  not not_62 (not_62_out, CS1);
  not not_63 (not_63_out, CS2);
  not not_64 (not_64_out, CS3);
  not not_65 (not_65_out, O1);
  not not_66 (not_66_out, CS1);
  not not_67 (not_67_out, CS2);
  not not_68 (not_68_out, CS3);
  not not_69 (not_69_out, CS0);
  not not_70 (not_70_out, CS2);
  not not_71 (not_71_out, CS3);
  not not_72 (not_72_out, O0);
  not not_73 (not_73_out, O1);
  not not_74 (not_74_out, O2);
  not not_75 (not_75_out, O3);
  not not_76 (not_76_out, CS0);
  not not_77 (not_77_out, CS2);
  not not_78 (not_78_out, CS3);
  not not_79 (not_79_out, O1);
  not not_80 (not_80_out, O2);
  not not_81 (not_81_out, O3);
  not not_82 (not_82_out, CS0);
  not not_83 (not_83_out, CS2);
  not not_84 (not_84_out, CS3);
  not not_85 (not_85_out, O0);
  not not_86 (not_86_out, O2);
  not not_87 (not_87_out, O3);
  not not_88 (not_88_out, CS0);
  not not_89 (not_89_out, CS1);
  not not_90 (not_90_out, CS2);
  not not_91 (not_91_out, CS3);
  not not_92 (not_92_out, CS0);
  not not_93 (not_93_out, CS1);
  not not_94 (not_94_out, CS2);
  not not_95 (not_95_out, CS3);
  and and_1 (and_1_out, not_88_out, not_89_out, 1'b1, not_90_out, not_91_out);
  and and_2 (and_2_out, CS0, not_1_out, not_2_out, not_3_out, 1'b1, not_4_out, not_5_out, not_6_out, O3);
  and and_3 (and_3_out, CS0, not_7_out, not_8_out, not_9_out, 1'b1, O0, not_10_out, not_11_out, O3);
  and and_4 (and_4_out, CS0, not_12_out, not_13_out, not_14_out, 1'b1, O0, O1, not_15_out, O3);
  and and_5 (and_5_out, CS0, not_16_out, not_17_out, not_18_out, O0, not_19_out, O2, O3, Z);
  and and_6 (and_6_out, CS0, not_20_out, not_21_out, not_22_out, O0, O1, O2, O3, C);
  and and_7 (and_7_out, not_23_out, CS1, not_24_out, 1'b1, not_25_out, not_26_out, not_27_out, not_28_out, not_29_out);
  and and_8 (and_8_out, not_30_out, CS1, not_31_out, 1'b1, not_32_out, O0, not_33_out, not_34_out, not_35_out);
  and and_9 (and_9_out, not_36_out, CS1, not_37_out, 1'b1, not_38_out, not_39_out, O1, not_40_out, not_41_out);
  and and_10 (and_10_out, not_42_out, CS1, not_43_out, 1'b1, not_44_out, O0, O1, not_45_out, not_46_out);
  and and_11 (and_11_out, not_92_out, not_93_out, 1'b1, not_94_out, not_95_out);
  and and_12 (and_12_out, CS0, not_47_out, not_48_out, not_49_out, 1'b1, not_50_out, not_51_out, not_52_out, O3);
  and and_13 (and_13_out, CS0, not_53_out, not_54_out, not_55_out, 1'b1, O0, not_56_out, not_57_out, O3);
  and and_14 (and_14_out, CS0, not_58_out, not_59_out, not_60_out, 1'b1, O0, O1, not_61_out, O3);
  and and_15 (and_15_out, CS0, not_62_out, not_63_out, not_64_out, O0, not_65_out, O2, O3, Z);
  and and_16 (and_16_out, CS0, not_66_out, not_67_out, not_68_out, O0, O1, O2, O3, C);
  and and_17 (and_17_out, not_69_out, CS1, not_70_out, 1'b1, not_71_out, not_72_out, not_73_out, not_74_out, not_75_out);
  and and_18 (and_18_out, not_76_out, CS1, not_77_out, 1'b1, not_78_out, O0, not_79_out, not_80_out, not_81_out);
  and and_19 (and_19_out, not_82_out, CS1, not_83_out, 1'b1, not_84_out, not_85_out, O1, not_86_out, not_87_out);
  or or_1 (or_1_out, and_1_out, and_2_out, and_3_out, and_4_out, and_5_out, and_6_out, and_7_out);
  or or_2 (or_2_out, and_8_out, and_9_out, and_10_out, 1'b0, and_11_out, and_12_out, and_13_out);
  or or_3 (or_3_out, and_14_out, and_15_out, and_16_out, 1'b0, and_17_out, and_18_out, and_19_out);
  or or_4 (NS0, or_1_out, or_2_out, or_3_out);
endmodule

module NS0a (
  input  CS0,
  input  CS1,
  input  CS2,
  input  CS3,
  input  O0,
  input  O1,
  input  O2,
  input  O3,
  input  Z,
  input  M,
  input  C,
  output NS0
);

  wire and_1_out, and_2_out, and_3_out, and_4_out, and_5_out, and_6_out, and_7_out, not_1_out, not_2_out,
       not_3_out, not_4_out, not_5_out, not_6_out, not_7_out, not_8_out, not_9_out, not_10_out, not_11_out,
       not_12_out, not_13_out, not_14_out, not_15_out, not_16_out, not_17_out, not_18_out, not_19_out,
       not_20_out, not_21_out, not_22_out, not_23_out, not_24_out, not_25_out, not_26_out, not_27_out,
       not_28_out, not_29_out;

  not not_1 (not_1_out, CS1);
  not not_2 (not_2_out, CS2);
  not not_3 (not_3_out, CS3);
  not not_4 (not_4_out, O1);
  not not_5 (not_5_out, O2);
  not not_6 (not_6_out, CS1);
  not not_7 (not_7_out, CS2);
  not not_8 (not_8_out, CS3);
  not not_9 (not_9_out, O2);
  not not_10 (not_10_out, CS1);
  not not_11 (not_11_out, CS2);
  not not_12 (not_12_out, CS3);
  not not_13 (not_13_out, O1);
  not not_14 (not_14_out, CS1);
  not not_15 (not_15_out, CS2);
  not not_16 (not_16_out, CS3);
  not not_17 (not_17_out, O0);
  not not_18 (not_18_out, CS1);
  not not_19 (not_19_out, CS2);
  not not_20 (not_20_out, CS3);
  not not_21 (not_21_out, CS1);
  not not_22 (not_22_out, CS2);
  not not_23 (not_23_out, CS3);
  not not_24 (not_24_out, O2);
  not not_25 (not_25_out, O3);
  not not_26 (not_26_out, CS0);
  not not_27 (not_27_out, CS1);
  not not_28 (not_28_out, CS2);
  not not_29 (not_29_out, CS3);
  and and_1 (and_1_out, not_26_out, not_27_out, 1'b1, not_28_out, not_29_out);
  and and_2 (and_2_out, CS0, not_1_out, not_2_out, not_3_out, not_4_out, not_5_out, O3);
  and and_3 (and_3_out, CS0, not_6_out, not_7_out, not_8_out, 1'b1, O0, O1, not_9_out, O3);
  and and_4 (and_4_out, CS0, not_10_out, not_11_out, not_12_out, O0, not_13_out, O2, O3, Z);
  and and_5 (and_5_out, CS0, not_14_out, not_15_out, not_16_out, not_17_out, O1, O2, O3, M);
  and and_6 (and_6_out, CS0, not_18_out, not_19_out, not_20_out, O0, O1, O2, O3, C);
  and and_7 (and_7_out, CS0, not_21_out, not_22_out, 1'b1, not_23_out, not_24_out, not_25_out);
  or or_1 (NS0, and_1_out, and_2_out, and_3_out, and_4_out, and_5_out, and_6_out, and_7_out);
endmodule
