// Logisim project instruction register.circ as structural Verilog: 1 circuit, main circuit main
module main (
  input  CLK,
  input  WRITE_IR,
  input  [9:0] DATA_IN,
  output [3:0] opcode,
  output [5:0] oprand
);

  wire and_1_out;

  and and_1 (and_1_out, CLK, WRITE_IR);
  D_Flip_Flop #(.trigger("falling")) d_ff_1 (
    .clk(and_1_out), .D(DATA_IN[9]), .Q(opcode[3]));  // open: Qn, preset, en, reset
  D_Flip_Flop #(.trigger("falling")) d_ff_2 (
    .clk(and_1_out), .D(DATA_IN[8]), .Q(opcode[2]));  // open: Qn, preset, en, reset
  D_Flip_Flop #(.trigger("falling")) d_ff_3 (
    .clk(and_1_out), .D(DATA_IN[7]), .Q(opcode[1]));  // open: Qn, preset, en, reset
  D_Flip_Flop #(.trigger("falling")) d_ff_4 (
    .clk(and_1_out), .D(DATA_IN[6]), .Q(opcode[0]));  // open: Qn, preset, en, reset
  D_Flip_Flop #(.trigger("falling")) d_ff_5 (
    .clk(and_1_out), .D(DATA_IN[5]), .Q(oprand[5]));  // open: Qn, preset, en, reset
  D_Flip_Flop #(.trigger("falling")) d_ff_6 (
    .clk(and_1_out), .D(DATA_IN[4]), .Q(oprand[4]));  // open: Qn, preset, en, reset
  D_Flip_Flop #(.trigger("falling")) d_ff_7 (
    .clk(and_1_out), .D(DATA_IN[3]), .Q(oprand[3]));  // open: Qn, preset, en, reset
  D_Flip_Flop #(.trigger("falling")) d_ff_8 (
    .clk(and_1_out), .D(DATA_IN[2]), .Q(oprand[2]));  // open: Qn, preset, en, reset
  D_Flip_Flop #(.trigger("falling")) d_ff_9 (
    .clk(and_1_out), .D(DATA_IN[1]), .Q(oprand[1]));  // open: Qn, preset, en, reset
  D_Flip_Flop #(.trigger("falling")) d_ff_10 (
    .clk(and_1_out), .D(DATA_IN[0]), .Q(oprand[0]));  // open: Qn, preset, en, reset

  // Notes on the sheet:
  //   DATA_IN: pull=up
  //   INSTRUCTION REGISTER
endmodule
