// Logisim project program counter.circ as structural Verilog: 1 circuit, main circuit main
module main (
  input  in_1,
  input  WRITEpc,
  input  [5:0] DATA_IN,
  output [5:0] DATA_OUT
);

  wire and_1_out;

  and and_1 (and_1_out, in_1, WRITEpc);
  D_Flip_Flop #(.trigger("falling")) d_ff_1 (
    .clk(and_1_out), .D(DATA_IN[0]), .Q(DATA_OUT[0]));  // open: Qn, preset, en, reset
  D_Flip_Flop #(.trigger("falling")) d_ff_2 (
    .clk(and_1_out), .D(DATA_IN[1]), .Q(DATA_OUT[1]));  // open: Qn, preset, en, reset
  D_Flip_Flop #(.trigger("falling")) d_ff_3 (
    .clk(and_1_out), .D(DATA_IN[2]), .Q(DATA_OUT[2]));  // open: Qn, preset, en, reset
  D_Flip_Flop #(.trigger("falling")) d_ff_4 (
    .clk(and_1_out), .D(DATA_IN[3]), .Q(DATA_OUT[3]));  // open: Qn, preset, en, reset
  D_Flip_Flop #(.trigger("falling")) d_ff_5 (
    .clk(and_1_out), .D(DATA_IN[4]), .Q(DATA_OUT[4]));  // open: Qn, preset, en, reset
  D_Flip_Flop #(.trigger("falling")) d_ff_6 (
    .clk(and_1_out), .D(DATA_IN[5]), .Q(DATA_OUT[5]));  // open: Qn, preset, en, reset

  // Notes on the sheet:
  //   DATA_IN: pull=up
  //   program counter
endmodule
