// Logisim project alu  control.circ as structural Verilog: 2 circuits, main circuit main
module main (
  input  [3:0] opcode,
  output [2:0] alu_control
);

  alu_control alu_control_1 (
    .op0(opcode[0]), .op1(opcode[1]), .op2(opcode[2]), .op3(opcode[3]), .o0(alu_control[0]),
    .o1(alu_control[1]), .o2(alu_control[2]));
endmodule

module alu_control (
  input  op0,
  input  op1,
  input  op2,
  input  op3,
  output o0,
  output o1,
  output o2
);

  wire and_1_out, and_2_out, and_3_out, and_4_out, and_5_out, not_1_out, not_2_out, not_3_out, not_4_out,
       not_5_out;

  not not_1 (not_1_out, op1);
  and and_1 (and_1_out, not_1_out, op2);
  and and_2 (and_2_out, op2, op3);
  not not_2 (not_2_out, op1);
  and and_3 (and_3_out, op2, not_3_out);
  not not_3 (not_3_out, op3);
  not not_4 (not_4_out, op2);
  and and_4 (and_4_out, not_4_out, op3);
  and and_5 (and_5_out, op1, op2, not_5_out);
  not not_5 (not_5_out, op3);
  or or_1 (o0, and_1_out, and_2_out);
  or or_2 (o1, not_2_out, and_3_out);
  or or_3 (o2, and_4_out, and_5_out);
endmodule
