// Logisim project ADVANCE MEMORY.circ as structural Verilog: 2 circuits, main circuit HI
module main (
);

  HI hi_1 ();  // open: ADRES, DATA_IN, WR, ZEROS, ONE, CLK, DATA_OUT
endmodule

module HI (
  input  [5:0] ADRES,
  input  [9:0] DATA_IN,
  input  WR,
  input  ZEROS,
  input  ONE,
  input  CLK,
  output [9:0] DATA_OUT
);

  wire not_1_out;

  not not_1 (not_1_out, CLK);
  RAM #(.addrWidth(6), .dataWidth(10), .bus("separate")) ram_1 (
    .addr(ADRES), .din(DATA_IN), .data(DATA_OUT), .str(WR), .sel(ONE), .clk(not_1_out), .ld(ONE), .clr(ZEROS));
endmodule
