// Logisim project MEMORY1.circ as structural Verilog
module main (
  input  clk,
  input  write,
  input  [5:0] write_addr,
  input  [5:0] read_add,
  input  [9:0] data_in,
  output [9:0] data_out
);

  wire and_1_out, and_2_out, and_3_out, and_4_out, and_5_out, and_6_out, and_7_out, and_8_out, and_9_out,
       and_10_out, and_11_out, and_12_out, and_13_out, and_14_out, and_15_out, and_16_out, and_17_out,
       and_18_out, and_19_out, and_20_out, and_21_out, and_22_out, and_23_out, and_24_out, and_25_out,
       and_26_out, and_27_out, and_28_out, and_29_out, and_30_out, and_31_out, and_32_out, and_33_out,
       and_34_out, and_35_out, and_36_out, and_37_out, and_38_out, and_39_out, and_40_out, and_41_out,
       and_42_out, and_43_out, and_44_out, and_45_out, and_46_out, and_47_out, and_48_out, and_49_out,
       and_50_out, and_51_out, and_52_out, and_53_out, and_54_out, and_55_out, and_56_out, and_57_out,
       and_58_out, and_59_out, and_60_out, and_61_out, and_62_out, and_63_out, and_64_out, decorderic_1_i0,
       decorderic_1_i1, decorderic_1_i3, decorderic_1_out_5, decorderic_1_out_6, decorderic_1_out_7,
       decorderic_1_out_8, decorderic_1_out_9, decorderic_1_out_10, decorderic_1_out_11, decorderic_1_out_12,
       decorderic_1_out_13, decorderic_1_out_14, decorderic_1_out_15, decorderic_1_out_16,
       decorderic_1_out_17, decorderic_2_out_18, decorderic_2_out_19, decorderic_2_out_20,
       decorderic_2_out_21, decorderic_2_out_22, decorderic_2_out_23, decorderic_2_out_24,
       decorderic_2_out_25, decorderic_2_out_26, decorderic_2_out_27, decorderic_2_out_28,
       decorderic_2_out_29, decorderic_2_out_30, decorderic_2_out_31, decorderic_2_out_32,
       decorderic_2_out_33, decorderic_3_out_34, decorderic_3_out_35, decorderic_3_out_36,
       decorderic_3_out_37, decorderic_3_out_38, decorderic_3_out_39, decorderic_3_out_40,
       decorderic_3_out_41, decorderic_3_out_42, decorderic_3_out_43, decorderic_3_out_44,
       decorderic_3_out_45, decorderic_3_out_46, decorderic_3_out_47, decorderic_3_out_48,
       decorderic_3_out_49, decorderic_4_out_50, decorderic_4_out_51, decorderic_4_out_52,
       decorderic_4_out_53, decorderic_4_out_54, decorderic_4_out_55, decorderic_4_out_56,
       decorderic_4_out_57, decorderic_4_out_58, decorderic_4_out_59, decorderic_4_out_60,
       decorderic_4_out_61, decorderic_4_out_62, decorderic_4_out_63, decorderic_4_out_64,
       decorderic_4_out_65;
  wire [9:0] memory_1_data_out, memory_2_data_out, memory_3_data_out, memory_4_data_out, memory_5_data_out,
       memory_6_data_out, memory_7_data_out, memory_8_data_out, memory_9_data_out, memory_10_data_out,
       memory_11_data_out, memory_12_data_out, memory_13_data_out, memory_14_data_out, memory_15_data_out,
       memory_16_data_out, memory_17_data_out, memory_18_data_out, memory_19_data_out, memory_20_data_out,
       memory_21_data_out, memory_22_data_out, memory_23_data_out, memory_24_data_out, memory_25_data_out,
       memory_26_data_out, memory_27_data_out, memory_28_data_out, memory_29_data_out, memory_30_data_out,
       memory_31_data_out, memory_32_data_out, memory_33_data_out, memory_34_data_out, memory_35_data_out,
       memory_36_data_out, memory_37_data_out, memory_38_data_out, memory_39_data_out, memory_40_data_out,
       memory_41_data_out, memory_42_data_out, memory_43_data_out, memory_44_data_out, memory_45_data_out,
       memory_46_data_out, memory_47_data_out, memory_48_data_out, memory_49_data_out, memory_50_data_out,
       memory_51_data_out, memory_52_data_out, memory_53_data_out, memory_54_data_out, memory_55_data_out,
       memory_56_data_out, memory_57_data_out, memory_58_data_out, memory_59_data_out, memory_60_data_out,
       memory_61_data_out, memory_62_data_out, memory_63_data_out, memory_64_data_out, multiplexer_1_out,
       multiplexer_2_out, multiplexer_3_out, multiplexer_4_out;

  decorderic decorderic_1 (
    .in_1(write_addr), .i0(decorderic_1_i0), .i1(decorderic_1_i1), .i3(decorderic_1_i3),
    .out_5(decorderic_1_out_5), .out_6(decorderic_1_out_6), .out_7(decorderic_1_out_7),
    .out_8(decorderic_1_out_8), .out_9(decorderic_1_out_9), .out_10(decorderic_1_out_10),
    .out_11(decorderic_1_out_11), .out_12(decorderic_1_out_12), .out_13(decorderic_1_out_13),
    .out_14(decorderic_1_out_14), .out_15(decorderic_1_out_15), .out_16(decorderic_1_out_16),
    .out_17(decorderic_1_out_17));  // open: out_18, out_19, out_20, out_21, out_22, out_23, out_24, out_25, out_26, out_27, out_28, out_29, out_30, out_31, out_32, out_33, out_34, out_35, out_36, out_37, out_38, out_39, out_40, out_41, out_42, out_43, out_44, out_45, out_46, out_47, out_48, out_49, out_50, out_51, out_52, out_53, out_54, out_55, out_56, out_57, out_58, out_59, out_60, out_61, out_62, out_63, out_64, out_65
  decorderic decorderic_2 (
    .in_1(write_addr), .out_18(decorderic_2_out_18), .out_19(decorderic_2_out_19),
    .out_20(decorderic_2_out_20), .out_21(decorderic_2_out_21), .out_22(decorderic_2_out_22),
    .out_23(decorderic_2_out_23), .out_24(decorderic_2_out_24), .out_25(decorderic_2_out_25),
    .out_26(decorderic_2_out_26), .out_27(decorderic_2_out_27), .out_28(decorderic_2_out_28),
    .out_29(decorderic_2_out_29), .out_30(decorderic_2_out_30), .out_31(decorderic_2_out_31),
    .out_32(decorderic_2_out_32), .out_33(decorderic_2_out_33));  // open: i0, i1, i3, out_5, out_6, out_7, out_8, out_9, out_10, out_11, out_12, out_13, out_14, out_15, out_16, out_17, out_34, out_35, out_36, out_37, out_38, out_39, out_40, out_41, out_42, out_43, out_44, out_45, out_46, out_47, out_48, out_49, out_50, out_51, out_52, out_53, out_54, out_55, out_56, out_57, out_58, out_59, out_60, out_61, out_62, out_63, out_64, out_65
  decorderic decorderic_3 (
    .in_1(write_addr), .out_34(decorderic_3_out_34), .out_35(decorderic_3_out_35),
    .out_36(decorderic_3_out_36), .out_37(decorderic_3_out_37), .out_38(decorderic_3_out_38),
    .out_39(decorderic_3_out_39), .out_40(decorderic_3_out_40), .out_41(decorderic_3_out_41),
    .out_42(decorderic_3_out_42), .out_43(decorderic_3_out_43), .out_44(decorderic_3_out_44),
    .out_45(decorderic_3_out_45), .out_46(decorderic_3_out_46), .out_47(decorderic_3_out_47),
    .out_48(decorderic_3_out_48), .out_49(decorderic_3_out_49));  // open: i0, i1, i3, out_5, out_6, out_7, out_8, out_9, out_10, out_11, out_12, out_13, out_14, out_15, out_16, out_17, out_18, out_19, out_20, out_21, out_22, out_23, out_24, out_25, out_26, out_27, out_28, out_29, out_30, out_31, out_32, out_33, out_50, out_51, out_52, out_53, out_54, out_55, out_56, out_57, out_58, out_59, out_60, out_61, out_62, out_63, out_64, out_65
  decorderic decorderic_4 (
    .in_1(write_addr), .out_50(decorderic_4_out_50), .out_51(decorderic_4_out_51),
    .out_52(decorderic_4_out_52), .out_53(decorderic_4_out_53), .out_54(decorderic_4_out_54),
    .out_55(decorderic_4_out_55), .out_56(decorderic_4_out_56), .out_57(decorderic_4_out_57),
    .out_58(decorderic_4_out_58), .out_59(decorderic_4_out_59), .out_60(decorderic_4_out_60),
    .out_61(decorderic_4_out_61), .out_62(decorderic_4_out_62), .out_63(decorderic_4_out_63),
    .out_64(decorderic_4_out_64), .out_65(decorderic_4_out_65));  // open: i0, i1, i3, out_5, out_6, out_7, out_8, out_9, out_10, out_11, out_12, out_13, out_14, out_15, out_16, out_17, out_18, out_19, out_20, out_21, out_22, out_23, out_24, out_25, out_26, out_27, out_28, out_29, out_30, out_31, out_32, out_33, out_34, out_35, out_36, out_37, out_38, out_39, out_40, out_41, out_42, out_43, out_44, out_45, out_46, out_47, out_48, out_49
  and and_1 (and_1_out, write, decorderic_1_i0);
  and and_2 (and_2_out, decorderic_1_i1, write);
  and and_3 (and_3_out, decorderic_1_i3, write);
  and and_4 (and_4_out, decorderic_1_out_5, write);
  and and_5 (and_5_out, decorderic_1_out_6, write);
  and and_6 (and_6_out, decorderic_1_out_7, write);
  and and_7 (and_7_out, decorderic_1_out_8, write);
  and and_8 (and_8_out, decorderic_1_out_9, write);
  and and_9 (and_9_out, decorderic_1_out_10, write);
  and and_10 (and_10_out, decorderic_1_out_11, write);
  and and_11 (and_11_out, decorderic_1_out_12, write);
  and and_12 (and_12_out, decorderic_1_out_13, write);
  and and_13 (and_13_out, decorderic_1_out_14, write);
  and and_14 (and_14_out, decorderic_1_out_15, write);
  and and_15 (and_15_out, decorderic_1_out_16, write);
  and and_16 (and_16_out, write, decorderic_1_out_17);
  and and_17 (and_17_out, write, decorderic_2_out_18);
  and and_18 (and_18_out, decorderic_2_out_19, write);
  and and_19 (and_19_out, decorderic_2_out_20, write);
  and and_20 (and_20_out, decorderic_2_out_21, write);
  and and_21 (and_21_out, decorderic_2_out_22, write);
  and and_22 (and_22_out, decorderic_2_out_23, write);
  and and_23 (and_23_out, decorderic_2_out_24, write);
  and and_24 (and_24_out, decorderic_2_out_25, write);
  and and_25 (and_25_out, decorderic_2_out_26, write);
  and and_26 (and_26_out, decorderic_2_out_27, write);
  and and_27 (and_27_out, decorderic_2_out_28, write);
  and and_28 (and_28_out, decorderic_2_out_29, write);
  and and_29 (and_29_out, decorderic_2_out_30, write);
  and and_30 (and_30_out, decorderic_2_out_31, write);
  and and_31 (and_31_out, decorderic_2_out_32, write);
  and and_32 (and_32_out, write, decorderic_2_out_33);
  and and_33 (and_33_out, write, decorderic_3_out_34);
  and and_34 (and_34_out, decorderic_3_out_35, write);
  and and_35 (and_35_out, decorderic_3_out_36, write);
  and and_36 (and_36_out, decorderic_3_out_37, write);
  and and_37 (and_37_out, decorderic_3_out_38, write);
  and and_38 (and_38_out, decorderic_3_out_39, write);
  and and_39 (and_39_out, decorderic_3_out_40, write);
  and and_40 (and_40_out, decorderic_3_out_41, write);
  and and_41 (and_41_out, decorderic_3_out_42, write);
  and and_42 (and_42_out, decorderic_3_out_43, write);
  and and_43 (and_43_out, decorderic_3_out_44, write);
  and and_44 (and_44_out, decorderic_3_out_45, write);
  and and_45 (and_45_out, decorderic_3_out_46, write);
  and and_46 (and_46_out, decorderic_3_out_47, write);
  and and_47 (and_47_out, decorderic_3_out_48, write);
  and and_48 (and_48_out, write, decorderic_3_out_49);
  and and_49 (and_49_out, write, decorderic_4_out_50);
  and and_50 (and_50_out, decorderic_4_out_51, write);
  and and_51 (and_51_out, decorderic_4_out_52, write);
  and and_52 (and_52_out, decorderic_4_out_53, write);
  and and_53 (and_53_out, decorderic_4_out_54, write);
  and and_54 (and_54_out, decorderic_4_out_55, write);
  and and_55 (and_55_out, decorderic_4_out_56, write);
  and and_56 (and_56_out, decorderic_4_out_57, write);
  and and_57 (and_57_out, decorderic_4_out_58, write);
  and and_58 (and_58_out, decorderic_4_out_59, write);
  and and_59 (and_59_out, decorderic_4_out_60, write);
  and and_60 (and_60_out, decorderic_4_out_61, write);
  and and_61 (and_61_out, decorderic_4_out_62, write);
  and and_62 (and_62_out, decorderic_4_out_63, write);
  and and_63 (and_63_out, decorderic_4_out_64, write);
  and and_64 (and_64_out, write, decorderic_4_out_65);
  MEMORY memory_1 (.CLK(clk), .WRITE(and_1_out), .DATA_IN(data_in), .DATA_OUT(memory_1_data_out));
  MEMORY memory_2 (.CLK(clk), .WRITE(and_2_out), .DATA_IN(data_in), .DATA_OUT(memory_2_data_out));
  MEMORY memory_3 (.CLK(clk), .WRITE(and_3_out), .DATA_IN(data_in), .DATA_OUT(memory_3_data_out));
  MEMORY memory_4 (.CLK(clk), .WRITE(and_4_out), .DATA_IN(data_in), .DATA_OUT(memory_4_data_out));
  MEMORY memory_5 (.CLK(clk), .WRITE(and_5_out), .DATA_IN(data_in), .DATA_OUT(memory_5_data_out));
  MEMORY memory_6 (.CLK(clk), .WRITE(and_6_out), .DATA_IN(data_in), .DATA_OUT(memory_6_data_out));
  MEMORY memory_7 (.CLK(clk), .WRITE(and_7_out), .DATA_IN(data_in), .DATA_OUT(memory_7_data_out));
  MEMORY memory_8 (.CLK(clk), .WRITE(and_8_out), .DATA_IN(data_in), .DATA_OUT(memory_8_data_out));
  MEMORY memory_9 (.CLK(clk), .WRITE(and_9_out), .DATA_IN(data_in), .DATA_OUT(memory_9_data_out));
  MEMORY memory_10 (.CLK(clk), .WRITE(and_10_out), .DATA_IN(data_in), .DATA_OUT(memory_10_data_out));
  MEMORY memory_11 (.CLK(clk), .WRITE(and_11_out), .DATA_IN(data_in), .DATA_OUT(memory_11_data_out));
  MEMORY memory_12 (.CLK(clk), .WRITE(and_12_out), .DATA_IN(data_in), .DATA_OUT(memory_12_data_out));
  MEMORY memory_13 (.CLK(clk), .WRITE(and_13_out), .DATA_IN(data_in), .DATA_OUT(memory_13_data_out));
  MEMORY memory_14 (.CLK(clk), .WRITE(and_14_out), .DATA_IN(data_in), .DATA_OUT(memory_14_data_out));
  MEMORY memory_15 (.CLK(clk), .WRITE(and_15_out), .DATA_IN(data_in), .DATA_OUT(memory_15_data_out));
  MEMORY memory_16 (.CLK(clk), .WRITE(and_16_out), .DATA_IN(data_in), .DATA_OUT(memory_16_data_out));
  MEMORY memory_17 (.CLK(clk), .WRITE(and_17_out), .DATA_IN(data_in), .DATA_OUT(memory_17_data_out));
  MEMORY memory_18 (.CLK(clk), .WRITE(and_18_out), .DATA_IN(data_in), .DATA_OUT(memory_18_data_out));
  MEMORY memory_19 (.CLK(clk), .WRITE(and_19_out), .DATA_IN(data_in), .DATA_OUT(memory_19_data_out));
  MEMORY memory_20 (.CLK(clk), .WRITE(and_20_out), .DATA_IN(data_in), .DATA_OUT(memory_20_data_out));
  MEMORY memory_21 (.CLK(clk), .WRITE(and_21_out), .DATA_IN(data_in), .DATA_OUT(memory_21_data_out));
  MEMORY memory_22 (.CLK(clk), .WRITE(and_22_out), .DATA_IN(data_in), .DATA_OUT(memory_22_data_out));
  MEMORY memory_23 (.CLK(clk), .WRITE(and_23_out), .DATA_IN(data_in), .DATA_OUT(memory_23_data_out));
  MEMORY memory_24 (.CLK(clk), .WRITE(and_24_out), .DATA_IN(data_in), .DATA_OUT(memory_24_data_out));
  MEMORY memory_25 (.CLK(clk), .WRITE(and_25_out), .DATA_IN(data_in), .DATA_OUT(memory_25_data_out));
  MEMORY memory_26 (.CLK(clk), .WRITE(and_26_out), .DATA_IN(data_in), .DATA_OUT(memory_26_data_out));
  MEMORY memory_27 (.CLK(clk), .WRITE(and_27_out), .DATA_IN(data_in), .DATA_OUT(memory_27_data_out));
  MEMORY memory_28 (.CLK(clk), .WRITE(and_28_out), .DATA_IN(data_in), .DATA_OUT(memory_28_data_out));
  MEMORY memory_29 (.CLK(clk), .WRITE(and_29_out), .DATA_IN(data_in), .DATA_OUT(memory_29_data_out));
  MEMORY memory_30 (.CLK(clk), .WRITE(and_30_out), .DATA_IN(data_in), .DATA_OUT(memory_30_data_out));
  MEMORY memory_31 (.CLK(clk), .WRITE(and_31_out), .DATA_IN(data_in), .DATA_OUT(memory_31_data_out));
  MEMORY memory_32 (.CLK(clk), .WRITE(and_32_out), .DATA_IN(data_in), .DATA_OUT(memory_32_data_out));
  MEMORY memory_33 (.CLK(clk), .WRITE(and_33_out), .DATA_IN(data_in), .DATA_OUT(memory_33_data_out));
  MEMORY memory_34 (.CLK(clk), .WRITE(and_34_out), .DATA_IN(data_in), .DATA_OUT(memory_34_data_out));
  MEMORY memory_35 (.CLK(clk), .WRITE(and_35_out), .DATA_IN(data_in), .DATA_OUT(memory_35_data_out));
  MEMORY memory_36 (.CLK(clk), .WRITE(and_36_out), .DATA_IN(data_in), .DATA_OUT(memory_36_data_out));
  MEMORY memory_37 (.CLK(clk), .WRITE(and_37_out), .DATA_IN(data_in), .DATA_OUT(memory_37_data_out));
  MEMORY memory_38 (.CLK(clk), .WRITE(and_38_out), .DATA_IN(data_in), .DATA_OUT(memory_38_data_out));
  MEMORY memory_39 (.CLK(clk), .WRITE(and_39_out), .DATA_IN(data_in), .DATA_OUT(memory_39_data_out));
  MEMORY memory_40 (.CLK(clk), .WRITE(and_40_out), .DATA_IN(data_in), .DATA_OUT(memory_40_data_out));
  MEMORY memory_41 (.CLK(clk), .WRITE(and_41_out), .DATA_IN(data_in), .DATA_OUT(memory_41_data_out));
  MEMORY memory_42 (.CLK(clk), .WRITE(and_42_out), .DATA_IN(data_in), .DATA_OUT(memory_42_data_out));
  MEMORY memory_43 (.CLK(clk), .WRITE(and_43_out), .DATA_IN(data_in), .DATA_OUT(memory_43_data_out));
  MEMORY memory_44 (.CLK(clk), .WRITE(and_44_out), .DATA_IN(data_in), .DATA_OUT(memory_44_data_out));
  MEMORY memory_45 (.CLK(clk), .WRITE(and_45_out), .DATA_IN(data_in), .DATA_OUT(memory_45_data_out));
  MEMORY memory_46 (.CLK(clk), .WRITE(and_46_out), .DATA_IN(data_in), .DATA_OUT(memory_46_data_out));
  MEMORY memory_47 (.CLK(clk), .WRITE(and_47_out), .DATA_IN(data_in), .DATA_OUT(memory_47_data_out));
  MEMORY memory_48 (.CLK(clk), .WRITE(and_48_out), .DATA_IN(data_in), .DATA_OUT(memory_48_data_out));
  MEMORY memory_49 (.CLK(clk), .WRITE(and_49_out), .DATA_IN(data_in), .DATA_OUT(memory_49_data_out));
  MEMORY memory_50 (.CLK(clk), .WRITE(and_50_out), .DATA_IN(data_in), .DATA_OUT(memory_50_data_out));
  MEMORY memory_51 (.CLK(clk), .WRITE(and_51_out), .DATA_IN(data_in), .DATA_OUT(memory_51_data_out));
  MEMORY memory_52 (.CLK(clk), .WRITE(and_52_out), .DATA_IN(data_in), .DATA_OUT(memory_52_data_out));
  MEMORY memory_53 (.CLK(clk), .WRITE(and_53_out), .DATA_IN(data_in), .DATA_OUT(memory_53_data_out));
  MEMORY memory_54 (.CLK(clk), .WRITE(and_54_out), .DATA_IN(data_in), .DATA_OUT(memory_54_data_out));
  MEMORY memory_55 (.CLK(clk), .WRITE(and_55_out), .DATA_IN(data_in), .DATA_OUT(memory_55_data_out));
  MEMORY memory_56 (.CLK(clk), .WRITE(and_56_out), .DATA_IN(data_in), .DATA_OUT(memory_56_data_out));
  MEMORY memory_57 (.CLK(clk), .WRITE(and_57_out), .DATA_IN(data_in), .DATA_OUT(memory_57_data_out));
  MEMORY memory_58 (.CLK(clk), .WRITE(and_58_out), .DATA_IN(data_in), .DATA_OUT(memory_58_data_out));
  MEMORY memory_59 (.CLK(clk), .WRITE(and_59_out), .DATA_IN(data_in), .DATA_OUT(memory_59_data_out));
  MEMORY memory_60 (.CLK(clk), .WRITE(and_60_out), .DATA_IN(data_in), .DATA_OUT(memory_60_data_out));
  MEMORY memory_61 (.CLK(clk), .WRITE(and_61_out), .DATA_IN(data_in), .DATA_OUT(memory_61_data_out));
  MEMORY memory_62 (.CLK(clk), .WRITE(and_62_out), .DATA_IN(data_in), .DATA_OUT(memory_62_data_out));
  MEMORY memory_63 (.CLK(clk), .WRITE(and_63_out), .DATA_IN(data_in), .DATA_OUT(memory_63_data_out));
  MEMORY memory_64 (.CLK(clk), .WRITE(and_64_out), .DATA_IN(data_in), .DATA_OUT(memory_64_data_out));
  Multiplexer #(.select(4), .width(10)) multiplexer_1 (
    .in0(memory_1_data_out), .in1(memory_2_data_out), .in2(memory_3_data_out), .in3(memory_4_data_out),
    .in4(memory_5_data_out), .in5(memory_6_data_out), .in6(memory_7_data_out), .in7(memory_8_data_out),
    .in8(memory_9_data_out), .in9(memory_10_data_out), .in10(memory_11_data_out), .in11(memory_12_data_out),
    .in12(memory_13_data_out), .in13(memory_14_data_out), .in14(memory_15_data_out),
    .in15(memory_16_data_out), .out(multiplexer_1_out), .sel(read_add[3:0]));
  Multiplexer #(.select(4), .width(10)) multiplexer_2 (
    .in0(memory_17_data_out), .in1(memory_18_data_out), .in2(memory_19_data_out), .in3(memory_20_data_out),
    .in4(memory_21_data_out), .in5(memory_22_data_out), .in6(memory_23_data_out), .in7(memory_24_data_out),
    .in8(memory_25_data_out), .in9(memory_26_data_out), .in10(memory_27_data_out), .in11(memory_28_data_out),
    .in12(memory_29_data_out), .in13(memory_30_data_out), .in14(memory_31_data_out),
    .in15(memory_32_data_out), .out(multiplexer_2_out), .sel(read_add[3:0]));
  Multiplexer #(.select(4), .width(10)) multiplexer_3 (
    .in0(memory_33_data_out), .in1(memory_34_data_out), .in2(memory_35_data_out), .in3(memory_36_data_out),
    .in4(memory_37_data_out), .in5(memory_38_data_out), .in6(memory_39_data_out), .in7(memory_40_data_out),
    .in8(memory_41_data_out), .in9(memory_42_data_out), .in10(memory_43_data_out), .in11(memory_44_data_out),
    .in12(memory_45_data_out), .in13(memory_46_data_out), .in14(memory_47_data_out),
    .in15(memory_48_data_out), .out(multiplexer_3_out), .sel(read_add[3:0]));
  Multiplexer #(.select(4), .width(10)) multiplexer_4 (
    .in0(memory_49_data_out), .in1(memory_50_data_out), .in2(memory_51_data_out), .in3(memory_52_data_out),
    .in4(memory_53_data_out), .in5(memory_54_data_out), .in6(memory_55_data_out), .in7(memory_56_data_out),
    .in8(memory_57_data_out), .in9(memory_58_data_out), .in10(memory_59_data_out), .in11(memory_60_data_out),
    .in12(memory_61_data_out), .in13(memory_62_data_out), .in14(memory_63_data_out),
    .in15(memory_64_data_out), .out(multiplexer_4_out), .sel(read_add[3:0]));
  Multiplexer #(.select(2), .width(10)) multiplexer_5 (
    .in0(multiplexer_1_out), .in1(multiplexer_2_out), .in2(multiplexer_3_out), .in3(multiplexer_4_out),
    .out(data_out), .sel(read_add[5:4]));
endmodule

module MEMORY (
  input  CLK,
  input  WRITE,
  input  [9:0] DATA_IN,
  output [9:0] DATA_OUT
);

  wire and_1_out;

  and and_1 (and_1_out, CLK, WRITE);
  D_Flip_Flop #(.trigger("falling")) d_ff_1 (
    .clk(and_1_out), .D(DATA_IN[0]), .Q(DATA_OUT[0]));  // open: Qn, preset, en, reset
  D_Flip_Flop #(.trigger("falling")) d_ff_2 (
    .clk(and_1_out), .D(DATA_IN[1]), .Q(DATA_OUT[1]));  // open: Qn, preset, en, reset
  D_Flip_Flop #(.trigger("falling")) d_ff_3 (
    .clk(and_1_out), .D(DATA_IN[2]), .Q(DATA_OUT[2]));  // open: Qn, preset, en, reset
  D_Flip_Flop #(.trigger("falling")) d_ff_4 (
    .clk(and_1_out), .D(DATA_IN[3]), .Q(DATA_OUT[3]));  // open: Qn, preset, en, reset
  D_Flip_Flop #(.trigger("falling")) d_ff_5 (
    .clk(and_1_out), .D(DATA_IN[4]), .Q(DATA_OUT[4]));  // open: Qn, preset, en, reset
  D_Flip_Flop #(.trigger("falling")) d_ff_6 (
    .clk(and_1_out), .D(DATA_IN[5]), .Q(DATA_OUT[5]));  // open: Qn, preset, en, reset
  D_Flip_Flop #(.trigger("falling")) d_ff_7 (
    .clk(and_1_out), .D(DATA_IN[6]), .Q(DATA_OUT[6]));  // open: Qn, preset, en, reset
  D_Flip_Flop #(.trigger("falling")) d_ff_8 (
    .clk(and_1_out), .D(DATA_IN[7]), .Q(DATA_OUT[7]));  // open: Qn, preset, en, reset
  D_Flip_Flop #(.trigger("falling")) d_ff_9 (
    .clk(and_1_out), .D(DATA_IN[8]), .Q(DATA_OUT[8]));  // open: Qn, preset, en, reset
  D_Flip_Flop #(.trigger("falling")) d_ff_10 (
    .clk(and_1_out), .D(DATA_IN[9]), .Q(DATA_OUT[9]));  // open: Qn, preset, en, reset

  // Notes on the sheet:
  //   DATA_IN: pull=up
endmodule

module _3X8decorder (
  input  a,
  input  b,
  input  c,
  input  e,
  output i0,
  output i1,
  output i2,
  output i3,
  output i4,
  output i5,
  output i6,
  output i7
);

  wire not_1_out, not_2_out, not_3_out, not_4_out, not_5_out, not_6_out, not_7_out, not_8_out, not_9_out,
       not_10_out, not_11_out, not_12_out;

  not not_1 (not_1_out, a);
  not not_2 (not_2_out, b);
  not not_3 (not_3_out, c);
  not not_4 (not_4_out, a);
  not not_5 (not_5_out, b);
  not not_6 (not_6_out, a);
  not not_7 (not_7_out, c);
  not not_8 (not_8_out, a);
  not not_9 (not_9_out, b);
  not not_10 (not_10_out, c);
  not not_11 (not_11_out, b);
  not not_12 (not_12_out, c);
  and and_1 (i7, a, b, 1'b1, c, e);
  and and_2 (i0, not_1_out, not_2_out, 1'b1, not_3_out, e);
  and and_3 (i1, not_4_out, not_5_out, 1'b1, c, e);
  and and_4 (i2, not_6_out, b, 1'b1, not_7_out, e);
  and and_5 (i3, not_8_out, b, 1'b1, c, e);
  and and_6 (i4, a, not_9_out, 1'b1, not_10_out, e);
  and and_7 (i5, a, not_11_out, 1'b1, c, e);
  and and_8 (i6, a, b, 1'b1, not_12_out, e);
endmodule

module decorderic (
  input  [5:0] in_1,
  output i0,
  output i1,
  output i3,
  output out_5,
  output out_6,
  output out_7,
  output out_8,
  output out_9,
  output out_10,
  output out_11,
  output out_12,
  output out_13,
  output out_14,
  output out_15,
  output out_16,
  output out_17,
  output out_18,
  output out_19,
  output out_20,
  output out_21,
  output out_22,
  output out_23,
  output out_24,
  output out_25,
  output out_26,
  output out_27,
  output out_28,
  output out_29,
  output out_30,
  output out_31,
  output out_32,
  output out_33,
  output out_34,
  output out_35,
  output out_36,
  output out_37,
  output out_38,
  output out_39,
  output out_40,
  output out_41,
  output out_42,
  output out_43,
  output out_44,
  output out_45,
  output out_46,
  output out_47,
  output out_48,
  output out_49,
  output out_50,
  output out_51,
  output out_52,
  output out_53,
  output out_54,
  output out_55,
  output out_56,
  output out_57,
  output out_58,
  output out_59,
  output out_60,
  output out_61,
  output out_62,
  output out_63,
  output out_64,
  output out_65
);

  wire decoder_1_out0, decoder_1_out1, decoder_1_out2, decoder_1_out3, decoder_1_out4, decoder_1_out5,
       decoder_1_out6, decoder_1_out7;

  Decoder #(.select(3), .tristate("false")) decoder_1 (
    .out0(decoder_1_out0), .out1(decoder_1_out1), .out2(decoder_1_out2), .out3(decoder_1_out3),
    .out4(decoder_1_out4), .out5(decoder_1_out5), .out6(decoder_1_out6), .out7(decoder_1_out7),
    .sel(in_1[5:3]));
  _3X8decorder u_3x8decorder_1 (
    .a(in_1[2]), .b(in_1[1]), .c(in_1[0]), .e(decoder_1_out0), .i0(i0), .i1(i1), .i2(i3), .i3(out_5),
    .i4(out_6), .i5(out_7), .i6(out_8), .i7(out_9));
  _3X8decorder u_3x8decorder_2 (
    .a(in_1[2]), .b(in_1[1]), .c(in_1[0]), .e(decoder_1_out1), .i0(out_10), .i1(out_11), .i2(out_12),
    .i3(out_13), .i4(out_14), .i5(out_15), .i6(out_16), .i7(out_17));
  _3X8decorder u_3x8decorder_3 (
    .a(in_1[2]), .b(in_1[1]), .c(in_1[0]), .e(decoder_1_out2), .i0(out_18), .i1(out_19), .i2(out_20),
    .i3(out_21), .i4(out_22), .i5(out_23), .i6(out_24), .i7(out_25));
  _3X8decorder u_3x8decorder_4 (
    .a(in_1[2]), .b(in_1[1]), .c(in_1[0]), .e(decoder_1_out3), .i0(out_26), .i1(out_27), .i2(out_28),
    .i3(out_29), .i4(out_30), .i5(out_31), .i6(out_32), .i7(out_33));
  _3X8decorder u_3x8decorder_5 (
    .a(in_1[2]), .b(in_1[1]), .c(in_1[0]), .e(decoder_1_out4), .i0(out_34), .i1(out_35), .i2(out_36),
    .i3(out_37), .i4(out_38), .i5(out_39), .i6(out_40), .i7(out_41));
  _3X8decorder u_3x8decorder_6 (
    .a(in_1[2]), .b(in_1[1]), .c(in_1[0]), .e(decoder_1_out5), .i0(out_42), .i1(out_43), .i2(out_44),
    .i3(out_45), .i4(out_46), .i5(out_47), .i6(out_48), .i7(out_49));
  _3X8decorder u_3x8decorder_7 (
    .a(in_1[2]), .b(in_1[1]), .c(in_1[0]), .e(decoder_1_out6), .i0(out_50), .i1(out_51), .i2(out_52),
    .i3(out_53), .i4(out_54), .i5(out_55), .i6(out_56), .i7(out_57));
  _3X8decorder u_3x8decorder_8 (
    .a(in_1[2]), .b(in_1[1]), .c(in_1[0]), .e(decoder_1_out7), .i0(out_58), .i1(out_59), .i2(out_60),
    .i3(out_61), .i4(out_62), .i5(out_63), .i6(out_64), .i7(out_65));
endmodule
